# Fritzing sketch smart garden system (saved by Fritzing 1.0.6)

parts:
  DHT2 = DHT11 Humitidy and Temperature Sensor (3 pins)
  WATER_PUMP1 = water pump/motor  # not connected
  Part3 = 5V Relay Module
  Part4 = LCD1602-I2C
  Part5 = ADS1115
  VCC1 = Battery
  ESP32_-_Back1 = ESP32 - CAM
  부품3 = FC-28 Soil Hygrometer Module - Probe  # not connected
  부품4 = FC-28 Soil Hygrometer Module  # not connected

nets:
  N1: DHT2.Signal, ESP32_-_Back1.GPIO4
  N2: Part3.S, ESP32_-_Back1.GPIO13
  VCC: Part3.VCC, ESP32_-_Back1.5V
  N3: Part3.-, ESP32_-_Back1.GND
  N4: Part3.Common, VCC1.+
  N5: Part4.SDA, Part5.SDA, ESP32_-_Back1.GPIO14
  N6: Part4.SCL, Part5.SCL, ESP32_-_Back1.GPIO15

custom parts:
  DHT11 Humitidy and Temperature Sensor (3 pins): DHT11 Humidity and Temperature Sensor (3 pins).
  water pump/motor: WATER PUMP BY ARDUBLOCKTR
  5V Relay Module: 5V Relay module
  LCD1602-I2C: A standard character display, usually with 2x16 characters. Comes in many colors with LCM1602 IIC attached.
  ADS1115: ADC ADS1115
  Battery: Your standard 2x 18650 battery pack (7,4 Volts)
  ESP32 - CAM: The ESP32-CAM has a very competitive small-size camera module that can operate independently as a minimum system with a footprint of only 27*40.5*4.5mm and a deep sleep current of up to 6mA.
  FC-28 Soil Hygrometer Module - Probe: The FC-28 is a soil hygrometer module that uses the Texas Instruments LM393 comparator chip to provide an analog measurement of soil humidity.
  FC-28 Soil Hygrometer Module: The FC-28 is a soil hygrometer module that uses the Texas Instruments LM393 comparator chip to provide an analog measurement of soil humidity. The digital output is high when soil moisture is over a certain threshold, as determined by adjusting the potentiometer.
